# Fritzing sketch photoresistor_LED (saved by Fritzing 0.9.8b)
breadboards: 1

parts:
  元件1 = Arduino Uno (Rev3)
  LED1 = LED - 5mm [color="Red (633nm)" current=0.030 package="5 mm [THT]"]
  R1 = Resistor [tolerance=±5% power=0.25 resistance=220 package=THT]
  R2 = Resistor [tolerance=±5% power=0.25 resistance=220 package=THT]
  R3 = Photocell (LDR) [package=THT]

nets:
  N1: 元件1.A0, R2.Pin_0, R3.pin_1
  N2: 元件1.D9_PWM, LED1.anode
  N3: 元件1.GND, R1.Pin_0, R2.Pin_1
  N4: 元件1.5V, R3.pin_0
  N5: LED1.cathode, R1.Pin_1
